# Fritzing sketch Digital_PID (saved by Fritzing 0.9.3b)
breadboards: 2

parts:
  LCD2004-I2C1 = LCD2004-I2C
  S2 = Pushbutton [package="[SMD]"]
  S3 = Pushbutton [package="[SMD]"]
  S4 = Pushbutton [package="[SMD]"]
  S5 = Pushbutton [package="[SMD]"]
  S6 = Pushbutton [package="[SMD]"]
  S7 = Pushbutton [package="[SMD]"]
  S8 = Pushbutton [package="[SMD]"]
  S9 = Pushbutton [package="[SMD]"]
  Part1 = Arduino Mega 2560 (Rev3)
  R1 = Resistor [tolerance=±5% resistance=220 package=THT]
  R2 = Resistor [tolerance=±5% resistance=220 package="1206 [SMD]"]
  R3 = Resistor [tolerance=±5% resistance=220 package="1206 [SMD]"]
  R4 = Resistor [tolerance=±5% resistance=220 package="1206 [SMD]"]
  R5 = Resistor [tolerance=±5% resistance=220 package="1206 [SMD]"]
  R6 = Resistor [tolerance=±5% resistance=220 package="1206 [SMD]"]
  R7 = Resistor [tolerance=±5% resistance=220 package="1206 [SMD]"]
  R8 = Resistor [tolerance=±5% resistance=220 package="1206 [SMD]"]
  Q1 = Basic FET N-Channel [package="D2Pak [SMD]"]
  R9 = Resistor [tolerance=±5% resistance=220 package="2010 [SMD]"]
  IC2 = Voltage Regulator [package=78xxl]
  C1 = Electrolytic Capacitor [capacitance=100µF package="200 mil [THT, electrolytic]"]
  C2 = Capacitor [package=cap-pth-small2]

nets:
  GND: LCD2004-I2C1.GND, Part1.GND, R1.Pin_0, R2.Pin_0, R3.Pin_0, R4.Pin_0, R5.Pin_0, R6.Pin_0, R7.Pin_0, R8.Pin_0, Q1.source, IC2.GND, C1.-, C2.2
  VCC: LCD2004-I2C1.VCC, S2.Pin_1, S2.Pin_2, S3.Pin_1, S3.Pin_2, S4.Pin_1, S4.Pin_2, S5.Pin_1, S5.Pin_2, S6.Pin_1, S6.Pin_2, S7.Pin_1, S7.Pin_2, S8.Pin_1, S8.Pin_2, S9.Pin_1, S9.Pin_2, Part1.5V, R9.Pin_0
  N1: LCD2004-I2C1.SDA, Part1.D20/SDA
  N2: LCD2004-I2C1.SCL, Part1.D21/SCL
  N3: S2.Pin_3, S2.Pin_4, Part1.D45, R2.Pin_1
  N4: S3.Pin_3, S3.Pin_4, Part1.D43, R6.Pin_1
  N5: S4.Pin_3, S4.Pin_4, Part1.D41, R8.Pin_1
  N6: S5.Pin_3, S5.Pin_4, Part1.D39, R1.Pin_1
  N7: S6.Pin_3, S6.Pin_4, Part1.D47, R7.Pin_1
  N8: S7.Pin_3, S7.Pin_4, Part1.D49, R3.Pin_1
  N9: S8.Pin_3, S8.Pin_4, Part1.D51, R4.Pin_1
  N10: S9.Pin_3, S9.Pin_4, Part1.D53, R5.Pin_1, Q1.drain
  N11: Part1.RESET, Q1.Gate, R9.Pin_1
  N12: Part1.VIN, IC2.OUT, C1.+, C2.1

notes:
  7809 Voltage Regulator
  100uF 25V Capacitor
  0.1uF Capacitor
  From 12V supply
  Modified Error Signal Input (E)
  Pin A4
  PWM Output (F)
  Pin 11
  20x4 LCD with I2C Interface
  Push Buttons for User Inputs

custom parts:
  LCD2004-I2C: A standard character display with 4x20 characters. Comes in many colors with LCM2004 IIC attached.
